// Logisim project Flip Flops.circ as structural Verilog
module SRFFNAND (
  input  S,
  input  R,
  output Q,
  output Qd
);

  wire not_1_out, not_2_out;

  not not_1 (not_1_out, S);
  not not_2 (not_2_out, R);
  nand nand_1 (Q, not_1_out, not_1_out, Qd);
  nand nand_2 (Qd, Q, not_2_out);

  // Notes on the sheet:
  //   The set-reset flip flop
endmodule

module SRFFNOR (
  input  S,
  input  R,
  output Q,
  output Qd
);

  wire nor_1_out, nor_2_out;

  nor nor_1 (nor_1_out, S, nor_2_out);
  nor nor_2 (nor_2_out, nor_1_out, R);
  not not_1 (Q, nor_1_out);
  not not_2 (Qd, nor_2_out);
endmodule
